# Fritzing sketch ButtonFloating_PullDown (saved by Fritzing 0.9.3b)
breadboards: 1

parts:
  부품1 = Arduino Uno (Rev3)
  R1 = Resistor [tolerance=±5% resistance=10k package=THT]
  S1 = Pushbutton [package="[THT]"]

nets:
  N1: 부품1.D2, R1.Pin_0, S1.Pin_1, S1.Pin_2
  N2: 부품1.5V, S1.Pin_3, S1.Pin_4
  N3: 부품1.GND, R1.Pin_1
