# Fritzing sketch ButtonFloating_PullUp (saved by Fritzing 0.9.3b)
breadboards: 1

parts:
  부품2 = Arduino Uno (Rev3)
  R2 = Resistor [tolerance=±5% resistance=10k package=THT]
  S2 = Pushbutton [package="[THT]"]

nets:
  N1: 부품2.D2, R2.Pin_0, S2.Pin_1, S2.Pin_2
  N2: 부품2.5V, R2.Pin_1
  N3: 부품2.GND, S2.Pin_3, S2.Pin_4
